# Fritzing sketch Sketch-Transmitter-board (saved by Fritzing 0.9.6b)
breadboards: 1

parts:
  Load_Cell1 = Load Cell - Red/white/black/green
  Part1 = HX711 Weighing Sensor Module
  Part2 = Arduino Uno (Rev3)
  U1 = RF-LINK_TX [package=rf-link_tx]
  Load_Cell2 = Load Cell - Red/white/black/green
  Load_Cell3 = Load Cell - Red/white/black/green
  Load_Cell4 = Load Cell - Red/white/black/green
  Part3 = HX711 Weighing Sensor Module
  Part4 = HX711 Weighing Sensor Module
  Part7 = HX711 Weighing Sensor Module
  DHT11_2 = DHT11 module  # not connected
  ANT1 = Antenna
  SW1 = DIP Switch 8 Position [package=dipswitch-08]  # not connected

nets:
  N1: Load_Cell1.wire1, Part1.E+
  N2: Load_Cell1.wire2, Part1.A+
  N3: Load_Cell1.wire3, Part1.E-
  N4: Load_Cell1.wire4, Part1.A-
  VCC: Part1.VCC, Part2.5V, U1.+5V, Part3.VCC, Part4.VCC, Part7.VCC
  GND: Part1.GND, Part2.A2, U1.GND, Part3.GND, Part4.GND, Part7.GND
  N5: Part1.DO/RX, Part2.D2
  N6: Part1.CK/TX, Part2.D3_PWM
  N7: Part2.D8, Part7.DO/RX
  N8: Part2.D9_PWM, Part7.CK/TX
  N9: Part2.D4, Part3.DO/RX
  N10: Part2.D5_PWM, Part3.CK/TX
  N11: Part2.D6_PWM, Part4.DO/RX
  N12: Part2.D7, Part4.CK/TX
  N13: U1.ANT, ANT1.antenna_lead
  N14: Load_Cell2.wire1, Part3.E+
  N15: Load_Cell2.wire2, Part3.A+
  N16: Load_Cell2.wire3, Part3.E-
  N17: Load_Cell2.wire4, Part3.A-
  N18: Load_Cell3.wire1, Part4.E+
  N19: Load_Cell3.wire2, Part4.A+
  N20: Load_Cell3.wire3, Part4.E-
  N21: Load_Cell3.wire4, Part4.A-
  N22: Load_Cell4.wire1, Part7.E+
  N23: Load_Cell4.wire2, Part7.A+
  N24: Load_Cell4.wire3, Part7.E-
  N25: Load_Cell4.wire4, Part7.A-

custom parts:
  Load Cell - Red/white/black/green: A rectangle load cell/weighting pressure Sensor with four wires - Red, white, black, green. Normally corresponding with E+, E-, A+, A- respectively.
  HX711 Weighing Sensor Module: HX711 is a precision 24-bit analog-to-digital converter (ADC) designed for weigh scales and industrial control applications to interface directly with a bridge sensor.
  DHT11 module: DHT11 black pcb module
